// Logisim project HCount.circ as structural Verilog: 5 circuits, main circuit VDP
module VDP (
);

  wire and_1_out, and_2_out, and_3_out, button_2_out, clock_1_out, d_ff_1_q, d_ff_2_q, d_ff_3_q,
       n7451_1_pin6, n7451_1_pin8, n74138_1_pin9, n74138_1_pin11, n74138_1_pin12, n74138_2_pin6,
       n74138_2_pin7, n74138_2_pin15, n74153_1_pin1, n74153_3_pin5, n74153_3_pin6, n74153_3_pin10,
       n74153_3_pin11, n74153_4_pin6, n74153_4_pin10, n74157_2_pin15, n74157_3_pin15, n74157_4_pin15,
       n74157_5_pin15, n74161_1_pin1, n74161_1_pin3, n74161_1_pin11, n74161_1_pin12, n74161_1_pin13,
       n74161_2_pin1, n74161_2_pin7, n74161_2_pin15, n74161_3_pin1, n74161_3_pin10, n74161_3_pin14,
       n74166_1_pin1, n74166_1_pin2, n74166_1_pin3, n74166_1_pin4, n74166_1_pin5, n74166_1_pin6,
       n74166_1_pin9, n74166_1_pin10, n74166_1_pin11, n74166_1_pin12, n74166_1_pin13, n74166_1_pin14,
       n74166_1_pin15, n74175_1_pin4, n74175_1_pin5, n74175_1_pin9, n74175_1_pin12, n74175_1_pin13,
       n74175_2_pin3, n74175_2_pin4, n74175_2_pin5, n74175_2_pin6, n74175_2_pin9, n74175_2_pin12,
       n74175_2_pin13, n74175_3_pin4, n74175_3_pin5, n74175_3_pin9, n74175_3_pin12, n74175_3_pin13,
       n74273_1_pin11, n74273_2_pin1, n74273_2_pin2, n74273_2_pin5, n74273_2_pin6, n74273_2_pin9,
       n74273_2_pin11, n74273_2_pin12, n74273_2_pin15, n74273_2_pin16, n74273_2_pin19, n74273_3_pin1,
       nand_1_out, nand_2_out, nand_3_out, nand_4_out, nand_5_out, nand_6_out, nand_7_out, nand_8_out,
       nand_9_out, nand_12_out, nor_1_out, nor_2_out, nor_4_out, nor_5_out, nor_6_out, nor_7_out, nor_8_out,
       nor_9_out, nor_10_out, nor_11_out, not_1_out, not_2_out, not_3_out, not_5_out, not_6_out, not_7_out,
       not_8_out, not_9_out, not_10_out, not_11_out, not_12_out, not_13_out, not_14_out, not_15_out,
       not_16_out, not_17_out, not_20_out, not_21_out, not_22_out, not_23_out, not_26_out, not_27_out,
       not_28_out, not_29_out, not_30_out, not_31_out, not_32_out, not_33_out, not_34_out, not_35_out,
       not_36_out, sn74ls393_2_qg, sn74ls393_2_qh;
  wire [2:0] not_4_out, sn74ls393_2_qa;
  wire [3:0] n74161_1_pin14, n74175_1_pin2;
  wire [5:0] sn74ls393_1_qa;
  wire [5:3] sn74ls393_2_qd;
  wire [7:0] multiplexer_2_out, multiplexer_3_out, n74157_2_pin3, n74273_1_pin3, n74273_2_pin3,
       rgb_video_1_p6, rom_1_data, rom_2_data;
  wire [7:2] n74161_2_pin5;
  wire [8:0] rgb_video_1_p4, rgb_video_1_p5;
  wire [15:0] n74157_1_pin4;

  Clock clock_1 (.out(clock_1_out));
  _74161 #(.ShowInternalStructure("true")) u_74161_1 (
    .pin1(n74161_1_pin1), .pin2(clock_1_out), .pin3(n74161_1_pin3), .pin4(n74161_1_pin3),
    .pin5(n74161_1_pin3), .pin6(n74161_1_pin3), .pin7(n74161_1_pin3), .pin14(n74161_1_pin14[0]),
    .pin13(n74161_1_pin13), .pin12(n74161_1_pin12), .pin11(n74161_1_pin11), .pin10(n74161_1_pin3),
    .pin9(n74161_1_pin3));  // open: pin15
  SN74LS393 sn74ls393_1 (
    .nCLK1(not_14_out), .CLR1(nor_2_out), .nCLK2(sn74ls393_1_qa[3]), .CLR2(nor_2_out),
    .QA(sn74ls393_1_qa[0]), .QB(sn74ls393_1_qa[1]), .QC(sn74ls393_1_qa[2]), .QD(sn74ls393_1_qa[3]),
    .QE(sn74ls393_1_qa[4]), .QF(sn74ls393_1_qa[5]));  // open: QG, QH
  SN74LS393 sn74ls393_2 (
    .nCLK1(not_9_out), .CLR1(not_12_out), .nCLK2(sn74ls393_2_qd[3]), .CLR2(not_12_out),
    .QA(sn74ls393_2_qa[0]), .QB(sn74ls393_2_qa[1]), .QC(sn74ls393_2_qa[2]), .QD(sn74ls393_2_qd[3]),
    .QE(sn74ls393_2_qd[4]), .QF(sn74ls393_2_qd[5]), .QG(sn74ls393_2_qg), .QH(sn74ls393_2_qh));
  not not_1 (not_1_out, sn74ls393_2_qh);
  D_Flip_Flop d_ff_1 (.clk(not_1_out), .D(1'b1), .Q(d_ff_1_q), .reset(not_2_out));  // open: Qn, preset
  not not_2 (not_2_out, nand_3_out);
  not not_3 (not_3_out, sn74ls393_2_qa[2]);
  and and_1 (and_1_out, n74161_1_pin11, n74161_1_pin12, n74161_1_pin13, n74161_1_pin14[0]);
  _74138 #(.ShowInternalStructure("true")) u_74138_1 (
    .pin1(sn74ls393_1_qa[1]), .pin2(sn74ls393_1_qa[3]), .pin3(sn74ls393_1_qa[4]), .pin4(sn74ls393_1_qa[2]),
    .pin5(sn74ls393_1_qa[2]), .pin6(sn74ls393_1_qa[5]), .pin12(n74138_1_pin12), .pin11(n74138_1_pin11),
    .pin9(n74138_1_pin9));  // open: pin7, pin15, pin14, pin13, pin10
  _74138 #(.ShowInternalStructure("true")) u_74138_2 (
    .pin1(sn74ls393_2_qd[3]), .pin2(sn74ls393_2_qd[4]), .pin3(sn74ls393_2_qg), .pin4(sn74ls393_2_qd[5]),
    .pin5(not_3_out), .pin6(n74138_2_pin6), .pin7(n74138_2_pin7), .pin15(n74138_2_pin15));  // open: pin14, pin13, pin12, pin11, pin10, pin9
  not not_4 (not_4_out[0], nand_1_out);
  nand nand_1 (nand_1_out, n74161_2_pin5[3], n74161_2_pin5[2]);
  not not_5 (not_5_out, n74161_2_pin5[3]);
  nand nand_2 (nand_2_out, not_5_out, n74161_2_pin5[2]);
  not not_6 (not_6_out, sn74ls393_1_qa[0]);
  nor nor_1 (nor_1_out, not_6_out, n74138_1_pin12);
  nor nor_2 (nor_2_out, not_6_out, n74138_1_pin9);
  not not_7 (not_7_out, sn74ls393_2_qa[1]);
  not not_8 (not_8_out, sn74ls393_2_qh);
  not not_9 (not_9_out, nor_1_out);
  not not_10 (not_10_out, d_ff_1_q);
  nor nor_3 (n74161_1_pin14[3], not_8_out, n74138_2_pin7);
  nor nor_4 (nor_4_out, not_7_out, n74138_2_pin15);
  not not_11 (not_11_out, n74157_1_pin4[7]);
  nand nand_3 (nand_3_out, d_ff_1_q, nor_4_out);
  _74161 #(.ShowInternalStructure("true")) u_74161_2 (
    .pin1(n74161_2_pin1), .pin2(not_11_out), .pin3(not_4_out[0]), .pin4(not_4_out[1]),
    .pin5(n74161_2_pin5[2]), .pin6(nand_2_out), .pin7(n74161_2_pin7), .pin15(n74161_2_pin15),
    .pin14(n74157_1_pin4[8]), .pin13(n74157_1_pin4[9]), .pin12(n74157_1_pin4[10]), .pin11(n74157_1_pin4[11]),
    .pin10(n74161_2_pin7), .pin9(nand_3_out));
  _74161 #(.ShowInternalStructure("true")) u_74161_3 (
    .pin1(n74161_3_pin1), .pin2(not_11_out), .pin3(n74161_2_pin5[4]), .pin4(n74161_2_pin5[5]),
    .pin5(n74161_2_pin5[6]), .pin6(n74161_2_pin5[7]), .pin7(n74161_2_pin15), .pin14(n74161_3_pin14),
    .pin13(n74157_1_pin4[13]), .pin12(n74157_1_pin4[14]), .pin11(n74157_1_pin4[15]), .pin10(n74161_3_pin10),
    .pin9(nand_3_out));  // open: pin15
  _74273 #(.ShowInternalStructure("true")) u_74273_1 (
    .pin2(not_4_out[2]), .pin3(n74273_1_pin3[0]), .pin4(n74273_1_pin3[1]), .pin5(not_4_out[1]),
    .pin6(n74161_2_pin5[2]), .pin7(n74273_1_pin3[2]), .pin8(n74273_1_pin3[3]), .pin9(n74161_2_pin5[3]),
    .pin19(n74161_2_pin5[7]), .pin18(n74273_1_pin3[7]), .pin17(n74273_1_pin3[6]), .pin16(n74161_2_pin5[6]),
    .pin15(n74161_2_pin5[5]), .pin14(n74273_1_pin3[5]), .pin13(n74273_1_pin3[4]), .pin12(n74161_2_pin5[4]),
    .pin11(n74273_1_pin11));  // open: pin1
  nand nand_4 (nand_4_out, sn74ls393_2_qh, sn74ls393_2_qg);
  not not_12 (not_12_out, nand_3_out);
  Button button_1 (.out(n74273_1_pin11));
  Timer_555 timer_555_1 (.Count(8'he0), .Trigger(not_9_out), .DOut(n74161_1_pin14[1]));
  not not_13 (not_13_out, sn74ls393_1_qa[0]);
  nand nand_5 (nand_5_out, nand_4_out, not_10_out);
  Timer_555 timer_555_2 (.Count(8'hf0), .Trigger(n74138_1_pin11), .DOut(n74161_1_pin14[2]));
  nor nor_5 (nor_5_out, not_13_out, n74161_1_pin11);
  D_Flip_Flop d_ff_2 (.clk(nor_5_out), .D(sn74ls393_1_qa[5]), .Q(d_ff_2_q));  // open: Qn, preset, reset
  not not_14 (not_14_out, n74161_1_pin11);
  not not_15 (not_15_out, not_4_out[1]);
  not not_16 (not_16_out, n74153_1_pin1);
  _74153 #(.ShowInternalStructure("true")) u_74153_1 (
    .pin1(n74153_1_pin1), .pin2(n74161_2_pin5[3]), .pin15(n74153_1_pin1), .pin14(n74161_2_pin5[2]),
    .pin13(sn74ls393_2_qd[5]), .pin12(sn74ls393_2_qd[4]), .pin11(sn74ls393_2_qd[3]),
    .pin10(sn74ls393_2_qa[2]), .pin9(n74157_1_pin4[7]));  // open: pin3, pin4, pin5, pin6, pin7
  nor nor_6 (nor_6_out, d_ff_2_q, nand_5_out);
  not not_17 (not_17_out, nor_6_out);
  _74157 #(.ShowInternalStructure("true")) u_74157_1 (
    .pin1(not_4_out[1]), .pin2(sn74ls393_1_qa[0]), .pin3(sn74ls393_1_qa[1]), .pin4(n74157_1_pin4[0]),
    .pin5(sn74ls393_1_qa[1]), .pin6(sn74ls393_1_qa[2]), .pin7(n74157_1_pin4[1]), .pin15(n74153_1_pin1),
    .pin14(sn74ls393_1_qa[3]), .pin13(sn74ls393_1_qa[4]), .pin12(n74157_1_pin4[3]),
    .pin11(sn74ls393_1_qa[2]), .pin10(sn74ls393_1_qa[3]), .pin9(n74157_1_pin4[2]));
  _7451 #(.ShowInternalStructure("true")) u_7451_1 (
    .pin1(not_15_out), .pin2(n74153_1_pin1), .pin3(sn74ls393_2_qd[3]), .pin4(not_16_out),
    .pin5(n74161_3_pin14), .pin6(n7451_1_pin6), .pin13(sn74ls393_1_qa[4]), .pin10(not_4_out[1]),
    .pin9(sn74ls393_2_qa[1]), .pin8(n7451_1_pin8));  // open: pin12, pin11
  nand nand_6 (nand_6_out, not_17_out, not_4_out[0]);
  not not_18 (n74157_1_pin4[4], n7451_1_pin8);
  _74153 #(.ShowInternalStructure("true")) u_74153_2 (
    .pin1(n74153_1_pin1), .pin2(n74161_2_pin5[3]), .pin3(sn74ls393_2_qd[4]), .pin4(sn74ls393_2_qd[3]),
    .pin5(sn74ls393_2_qa[2]), .pin6(sn74ls393_2_qa[1]), .pin7(n74157_1_pin4[6]), .pin15(n74153_1_pin1),
    .pin14(n74161_2_pin5[2]), .pin13(sn74ls393_2_qd[3]), .pin12(sn74ls393_2_qa[2]),
    .pin11(sn74ls393_2_qa[1]), .pin10(sn74ls393_2_qa[0]), .pin9(n74157_1_pin4[5]));
  not not_19 (n74157_1_pin4[12], n7451_1_pin6);
  nand nand_7 (nand_7_out, not_4_out[1], not_4_out[1]);
  nand nand_8 (nand_8_out, n74161_1_pin13, not_4_out[1]);
  nand nand_9 (nand_9_out, n74161_1_pin14[0], nand_7_out);
  _74175 #(.ShowInternalStructure("true")) u_74175_1 (
    .pin2(n74175_1_pin2[0]), .pin4(n74175_1_pin4), .pin5(n74175_1_pin5), .pin7(n74175_1_pin2[1]),
    .pin15(n74175_1_pin2[3]), .pin13(n74175_1_pin13), .pin12(n74175_1_pin12), .pin10(n74175_1_pin2[2]),
    .pin9(n74175_1_pin9));  // open: pin1, pin3, pin6, pin14, pin11
  nand nand_10 (n74175_1_pin9, nand_8_out, nand_9_out);
  _74273 #(.ShowInternalStructure("true")) u_74273_2 (
    .pin1(n74273_2_pin1), .pin2(n74273_2_pin2), .pin3(n74273_2_pin3[0]), .pin4(n74273_2_pin3[1]),
    .pin5(n74273_2_pin5), .pin6(n74273_2_pin6), .pin7(n74273_2_pin3[2]), .pin8(n74273_2_pin3[3]),
    .pin9(n74273_2_pin9), .pin19(n74273_2_pin19), .pin18(n74273_2_pin3[7]), .pin17(n74273_2_pin3[6]),
    .pin16(n74273_2_pin16), .pin15(n74273_2_pin15), .pin14(n74273_2_pin3[5]), .pin13(n74273_2_pin3[4]),
    .pin12(n74273_2_pin12), .pin11(n74273_2_pin11));
  not not_20 (not_20_out, n74161_1_pin14[0]);
  D_Flip_Flop d_ff_3 (.clk(not_20_out), .D(n74166_1_pin13), .Q(d_ff_3_q), .reset(not_21_out));  // open: Qn, preset
  not not_21 (not_21_out, not_4_out[2]);
  _74166 #(.ShowInternalStructure("true")) u_74166_1 (
    .pin1(n74166_1_pin1), .pin2(n74166_1_pin2), .pin3(n74166_1_pin3), .pin4(n74166_1_pin4),
    .pin5(n74166_1_pin5), .pin6(n74166_1_pin6), .pin7(not_20_out), .pin15(n74166_1_pin15),
    .pin14(n74166_1_pin14), .pin13(n74166_1_pin13), .pin12(n74166_1_pin12), .pin11(n74166_1_pin11),
    .pin10(n74166_1_pin10), .pin9(n74166_1_pin9));
  _74153 #(.ShowInternalStructure("true")) u_74153_3 (
    .pin1(not_17_out), .pin2(d_ff_3_q), .pin3(n74273_2_pin16), .pin4(n74273_2_pin6), .pin5(n74153_3_pin5),
    .pin6(n74153_3_pin6), .pin7(n74175_1_pin12), .pin15(not_17_out), .pin14(n74166_1_pin13),
    .pin13(n74273_2_pin19), .pin12(n74273_2_pin9), .pin11(n74153_3_pin11), .pin10(n74153_3_pin10),
    .pin9(n74175_1_pin13));
  _74175 #(.ShowInternalStructure("true")) u_74175_2 (
    .pin1(nand_6_out), .pin3(n74175_2_pin3), .pin4(n74175_2_pin4), .pin5(n74175_2_pin5),
    .pin6(n74175_2_pin6), .pin14(n74153_3_pin11), .pin13(n74175_2_pin13), .pin12(n74175_2_pin12),
    .pin11(n74153_3_pin5), .pin9(n74175_2_pin9));  // open: pin2, pin7, pin15, pin10
  _74157 #(.ShowInternalStructure("true")) u_74157_2 (
    .pin1(not_4_out[0]), .pin2(n74273_2_pin3[0]), .pin3(n74157_2_pin3[0]), .pin4(n74175_2_pin4),
    .pin5(n74273_2_pin3[1]), .pin6(n74157_2_pin3[1]), .pin7(n74175_2_pin5), .pin15(n74157_2_pin15),
    .pin14(n74273_2_pin3[3]), .pin13(n74157_2_pin3[3]), .pin12(n74175_2_pin13), .pin11(n74273_2_pin3[2]),
    .pin10(n74157_2_pin3[2]), .pin9(n74175_2_pin12));
  nand nand_11 (n74166_1_pin15, not_23_out, nand_12_out);
  not not_22 (not_22_out, and_1_out);
  not not_23 (not_23_out, not_22_out);
  _74153 #(.ShowInternalStructure("true")) u_74153_4 (
    .pin1(not_17_out), .pin2(d_ff_3_q), .pin3(n74273_2_pin12), .pin4(n74273_2_pin2), .pin5(n74175_2_pin3),
    .pin6(n74153_4_pin6), .pin7(n74175_1_pin4), .pin15(not_17_out), .pin14(n74166_1_pin13),
    .pin13(n74273_2_pin15), .pin12(n74273_2_pin5), .pin11(n74175_2_pin6), .pin10(n74153_4_pin10),
    .pin9(n74175_1_pin5));
  _74175 #(.ShowInternalStructure("true")) u_74175_3 (
    .pin1(nand_6_out), .pin2(n74153_4_pin6), .pin4(n74175_3_pin4), .pin5(n74175_3_pin5),
    .pin7(n74153_4_pin10), .pin15(n74153_3_pin10), .pin13(n74175_3_pin13), .pin12(n74175_3_pin12),
    .pin10(n74153_3_pin6), .pin9(n74175_3_pin9));  // open: pin3, pin6, pin14, pin11
  _74157 #(.ShowInternalStructure("true")) u_74157_3 (
    .pin1(not_4_out[0]), .pin2(n74273_2_pin3[4]), .pin3(n74157_2_pin3[0]), .pin4(n74175_3_pin4),
    .pin5(n74273_2_pin3[5]), .pin6(n74157_2_pin3[1]), .pin7(n74175_3_pin5), .pin15(n74157_3_pin15),
    .pin14(n74273_2_pin3[7]), .pin13(n74157_2_pin3[3]), .pin12(n74175_3_pin13), .pin11(n74273_2_pin3[6]),
    .pin10(n74157_2_pin3[2]), .pin9(n74175_3_pin12));
  // Random random_1: pin names not known; wires that end beside it: 1'b1, n74161_1_pin11
  not not_24 (n74175_2_pin9, nor_7_out);
  not not_25 (n74175_3_pin9, nor_8_out);
  nor nor_7 (nor_7_out, nor_9_out, button_2_out);
  nor nor_8 (nor_8_out, nor_10_out, button_2_out);
  nor nor_9 (nor_9_out, nand_12_out, n74157_2_pin3[4]);
  nor nor_10 (nor_10_out, nand_12_out, not_26_out);
  Button button_2 (.out(button_2_out));
  not not_26 (not_26_out, n74157_2_pin3[4]);
  nand nand_12 (nand_12_out, not_14_out, not_4_out[0], nor_11_out, n74157_2_pin3[7]);
  nor nor_11 (nor_11_out, n74157_2_pin3[5], n74157_2_pin3[6]);
  ROM #(.addrWidth(11)) rom_1 (.addr({n74157_2_pin3, sn74ls393_2_qa}), .data(rom_1_data));
  // Probe on n74157_1_pin4
  _74157 #(.ShowInternalStructure("true")) u_74157_4 (
    .pin1(not_4_out[0]), .pin2(n74157_2_pin3[4]), .pin3(rom_1_data[4]), .pin4(n74166_1_pin10),
    .pin5(n74157_2_pin3[5]), .pin6(rom_1_data[5]), .pin7(n74166_1_pin11), .pin15(n74157_4_pin15),
    .pin14(n74157_2_pin3[7]), .pin13(rom_1_data[7]), .pin12(n74166_1_pin14), .pin11(n74157_2_pin3[6]),
    .pin10(rom_1_data[6]), .pin9(n74166_1_pin12));
  _74157 #(.ShowInternalStructure("true")) u_74157_5 (
    .pin1(not_4_out[0]), .pin2(n74157_2_pin3[0]), .pin3(rom_1_data[0]), .pin4(n74166_1_pin2),
    .pin5(n74157_2_pin3[1]), .pin6(rom_1_data[1]), .pin7(n74166_1_pin3), .pin15(n74157_5_pin15),
    .pin14(n74157_2_pin3[3]), .pin13(rom_1_data[3]), .pin12(n74166_1_pin5), .pin11(n74157_2_pin3[2]),
    .pin10(rom_1_data[2]), .pin9(n74166_1_pin4));
  ROM #(.addrWidth(13)) rom_2 (.addr(n74157_1_pin4[12:0]), .data(rom_2_data));
  // Probe on n74157_1_pin4[12:0]
  _74273 #(.ShowInternalStructure("true")) u_74273_3 (
    .pin1(n74273_3_pin1), .pin2(n74157_2_pin3[0]), .pin3(rom_2_data[0]), .pin4(rom_2_data[1]),
    .pin5(n74157_2_pin3[1]), .pin6(n74157_2_pin3[2]), .pin7(rom_2_data[2]), .pin8(rom_2_data[3]),
    .pin9(n74157_2_pin3[3]), .pin19(n74157_2_pin3[7]), .pin18(rom_2_data[7]), .pin17(rom_2_data[6]),
    .pin16(n74157_2_pin3[6]), .pin15(n74157_2_pin3[5]), .pin14(rom_2_data[5]), .pin13(rom_2_data[4]),
    .pin12(n74157_2_pin3[4]), .pin11(n74161_1_pin11));
  // RGB_Video #(.cursor("No Cursor"), .height(262), .scale(1), .width(458)) rgb_video_1: pin names not known; wires that end beside it: 1'b0, n74161_1_pin14[0], 1'b1, rgb_video_1_p4, rgb_video_1_p5, rgb_video_1_p6
  Multiplexer #(.width(8)) multiplexer_1 (
    .in0(multiplexer_2_out), .in1(8'hc), .out(rgb_video_1_p6), .sel(n74161_1_pin14[3]));
  Multiplexer #(.width(8)) multiplexer_2 (
    .in0(multiplexer_3_out), .in1(8'hd), .out(multiplexer_2_out), .sel(n74161_1_pin14[1]));
  Multiplexer #(.width(8)) multiplexer_3 (
    .in0({4'b0000, n74175_1_pin2}), .in1(8'hb), .out(multiplexer_3_out), .sel(n74161_1_pin14[2]));
  Counter #(.max('h1ff), .width(9)) counter_1 (
    .load(1'b0), .count(1'b1), .Q(rgb_video_1_p5), .up(1'b1), .clk(n74161_1_pin14[1]), .clr(and_2_out));  // open: D, carry
  and and_2 (and_2_out, n74161_1_pin14[3], not_27_out);
  not not_27 (not_27_out, not_28_out);
  not not_28 (not_28_out, not_29_out);
  not not_29 (not_29_out, not_30_out);
  not not_30 (not_30_out, not_31_out);
  not not_31 (not_31_out, n74161_1_pin14[3]);
  Counter #(.max('h1ff), .width(9)) counter_2 (
    .load(1'b0), .count(1'b1), .Q(rgb_video_1_p4), .up(1'b1), .clk(n74161_1_pin14[0]), .clr(and_3_out));  // open: D, carry
  and and_3 (and_3_out, n74161_1_pin14[1], not_32_out);
  not not_32 (not_32_out, not_33_out);
  not not_33 (not_33_out, not_34_out);
  not not_34 (not_34_out, not_35_out);
  not not_35 (not_35_out, not_36_out);
  not not_36 (not_36_out, n74161_1_pin14[1]);
  // also tied to GND on the sheet: {n74273_1_pin3[0], n74273_1_pin3[2], n74273_1_pin3[5], n74273_1_pin3[6], n74273_1_pin3[7], n74153_1_pin1, n74166_1_pin1, n74166_1_pin6, n74273_2_pin11, n74157_2_pin15, n74157_3_pin15, n74157_4_pin15, n74157_5_pin15}
  // also tied to VCC on the sheet: {n74161_1_pin1, n74161_1_pin3, n74273_1_pin3[1], n74273_1_pin3[3], n74273_1_pin3[4], n74138_2_pin6, n74161_2_pin1, n74161_2_pin7, n74161_3_pin1, n74161_3_pin10, n74273_2_pin1, n74166_1_pin9, n74273_3_pin1}

  // Notes on the sheet:
  //   2 PSG
  //   12 Counter + Decode
  //   U33 74LS04 6x INV (4H 2V)
  //   U39 74LS04 6x INV (4V)
  //   U40 NE555 (H Sync)
  //   U41 NE555 (H Burst)
  //   U44 74LS00 4x 2-NAND
  //   U47 74LS04 6x INV
  //   11 Color Support
  //   U59 74LS166 Shift Register
  //   17 Bus and CPU
  //   U1 6502 CPU
  //   U9 MK4027 DRAM 1
  //   U10 MK4027 DRAM 2
  //   U11 MK4027 DRAM 3
  //   U12 MK4027 DRAM 4
  //   U13 MK4027 DRAM 5
  //   U14 MK4027 DRAM 6
  //   U15 MK4027 DRAM 7
  //   U16 MK4027 DRAM 8
  //   CLK
  //   14.31818 MHz
  //   U30 74LS393 8-bit Ripple Counter (H)
  //   U31 74LS138 1-of-8 (H Decode)
  //   U32 74LS02 4x 2-NOR (H & V)
  //   U34 74LS393 8-bit Ripple Counter (V)
  //   U35 74LS138 1-of-8 (V Decode)
  //   U36 74LS00 4x 2-NAND (V)
  //   U37 74LS74 2x D-FF (H & V)
  //   U38 74LS02 4x 2-NOR (Misc)
  //   8 Mode + Address Gen
  //   U42 74LS161 4-bit Counter (VC 0-3)
  //   U43 74LS161 4-bit Counter (VC 4-7)
  //   U45 74LS153 2x 1-of-4 (VMux)
  //   U46 74LS153 2x 1-of-4 (VMux)
  //   U67 74LS157 4-bit 1-of-2 (HMux)
  //   Uxx 74LS273 8-bit Register (Mode IO)
  //   U48 74LS175 4-bit D-FF (FG Attr)
  //   U49 74LS175 4-bit D-FF (BG Attr)
  //   U50 74LS157 4-bit 1-of-2 (FG Source)
  //   U51 74LS157 4-bit 1-of-2 (BG Source)
  //   U52 74LS273 8-bit Register (2BPP Palette)
  //   U53 74LS273 8-bit Register (VDP Latch)
  //   U54 74LS157 4-bit 1-of-2 (Char ROM Bypass)
  //   U55 74LS157 4-bit 1-of-2 (Char ROM Bypass)
  //   U56 74LS02 4x 2-NOR (Attrib Decode)
  //   U57 74LS20 2x 4-NAND (Attrib Decode)
  //   U58 SY2316 2Kx8 Character ROM
  //   6 Pixel Pipeline (Shielded Can)
  //   U60 74LS175 4-bit D-FF (DAC Latch)
  //   U61 74LS00 4x 2-NAND (Double-wide)
  //   U62 74LS74 2x D-FF (2BPP Decode)
  //   U63 74LS153 2x 1-of-4 (Color MUX)
  //   U64 74LS153 2x 1-of-4 (Color MUX 2BPP)
  //   2 Clock Generation (Shielded Can)
  //   U65 74LS161 4-bit Counter (Clock Divider)
  //   U66 74S04 4x INV (Clock Generator)
  //   U2 74LS257 4-bit -of-2 Tri-State (CPU Low)
  //   U3 74LS257 4-bit -of-2 Tri-State (CPU High)
  //   U4 74LS257 4-bit -of-2 Tri-State (VDP Low)
  //   U5 74LS257 4-bit -of-2 Tri-State (VDP High)
  //   U6 SY2316 2Kx8 mask ROM (System)
  //   U7 SY2316 2Kx8 mask ROM (BASIC 1)
  //   U8 SY2316 2Kx8 mask ROM (BASIC 2)
  //   U17 74LS138 1-of-8 (IO Decode)
  //   U18 74LS273 8-bit Register (Frequency)
  //   U19 74LS393 8-bit Ripple Counter (H)
  //   /CLK
  //   In Shielded Can
  //   nHsync
  //   U33E
  //   U57B
  //   U65
  //   (74LS393 is \edge triggered)
  //   6-bit H-Count
  //   \edge
  //   U30
  //   U34
  //   U37B
  //   active low
  //   Text
  //   HSel
  //   2Bpp
  //   ModeReg
  //   MUST update Address on /CLK mid-cycle
  //   [0-56]
  //   U33F
  //   U39F
  //   U44B
  //   7.15909 MHz
  //   3.579545 MHz
  //   1.7897725 MHz
  //   0.894886 MHz
  //   U31
  //   U39A
  //   U35
  //   and
  //   TextMode
  //   U39E
  //   U44A
  //   Work-around for incorrectly timed RCO output
  //   Not in BOM
  //   1 in 16
  //   U33B
  //   and
  //   U32A
  //   and
  //   U32B
  //   U39B
  //   and
  //   U32C
  //   and
  //   U32D
  //   and
  //   HSel
  //   U47A
  //   U33C
  //   and
  //   U36C
  //   falling edge
  //   V5432
  //   nHsync (43)
  //   101011
  //   nBurst (48)
  //   110000
  //   Rst (57)
  //   111001
  //   U39C
  //   Vsync (220)
  //   nRst
  //   VC 0-3
  //   U42
  //   VC 4-5
  //   U43
  //   1xxxx
  //   192
  //   nHide1
  //   and
  //   nHide2
  //   U36A
  //   Rst (262)
  //   U39D
  //   IOW_ VDP
  //   U40
  //   U33D
  //   and
  //   U38A
  //   Border (32)
  //   256
  //   or
  //   U36B
  //   nRst
  //   Can only load on a clock!
  //   HSync (4.7μs)
  //   Burst (2.8µs)
  //   U41
  //   /T=1.5
  //   nVvis
  //   Vsync
  //   V1
  //   U33A
  //   D1
  //   U37A
  //   V3
  //   Refresh
  //   Refresh
  //   Vsel0
  //   Vsel1
  //   nHvis
  //   and
  //   U38B
  //   HSel
  //   U47F
  //   nRefresh
  //   V5432
  //   U47B
  //   H4
  //   HCount
  //   U44C
  //   V1
  //   VC4
  //   U67
  //   U38D
  //   V4321
  //   V3210
  //   VDP Address
  //   U36D
  //   PCLK
  //   HSync
  //   Burst
  //   VSync
  //   nClrCol
  //   TextMode
  //   HSel
  //   Text
  //   HSel
  //   2Bpp
  //   Mode
  //   RCO (15)
  //   7.15909 MHz
  //   3.579545 MHz
  //   Video Out
  //   VDP Address
  //   Vcount
  //   U60
  //   Pixel Color
  //   nPCLK
  //   nWCLK
  //   In Shielded Can
  //   LATCH on /PWCLK edge
  //   DAC Latch
  //   In Shielded Can
  //   74LS00
  //   U61
  //   PWCLK
  //   U52
  //   COL2/3
  //   PCLK
  //   In Shielded Can
  //   U66F
  //   \PCLK
  //   2BPP
  //   nVisible
  //   U59
  //   2BPP D1
  //   U62
  //   Active Low
  //   Force Color 0
  //   SHIFT on \PCLK edge
  //   LOAD on \CLK at last \PCLK edge
  //   Shift Register
  //   nLd
  //   In Shielded Can
  //   IOQ_FE
  //   In Shielded Can
  //   nClrCol
  //   TextMode
  //   U63
  //   Col MUX 2,3
  //   U48
  //   U50
  //   FG MUX
  //   Last /PCLK before \CLK
  //   U44D
  //   In Shielded Can
  //   Y3
  //   Y2
  //   Delay beyond \PCLK edge
  //   nAttrLd (inhibit)
  //   Col MUX 0,1
  //   U49
  //   U51
  //   BG MUX
  //   In Shielded Can
  //   U64
  //   Y1
  //   Y0
  //   Text <- VDP
  //   Gfx <- DBus
  //   LoadQ on \CLK
  //   U47C
  //   U47D
  //   nAttrLd
  //   U56
  //   Ld8x
  //   or
  //   Ld9x
  //   or
  //   IO Load
  //   Palette
  //   and
  //   and
  //   IOW_FD
  //   n8x
  //   n9x
  //   U47E
  //   LoadQ on \CLK
  //   n8x/9x
  //   nAttrLd
  //   and
  //   U57A
  //   8x/9x (100x)
  //   Low 4 bits
  //   Bus CLK 0.89 MHz
  //   and
  //   U38C
  //   TextMode
  //   V[0..2]
  //   U58
  //   contents of rom_1 (hex, n*v repeats v):
  //   aa 55 aa 55 aa 55 aa 55 aa 41 aa 4 aa 10 aa 4 aa 0 aa 0 aa 0 aa 0 88 0 a2 0 24 0 8a 0 8 0 82 0 0 20
  //   2 4*0 1f 1f 18 18 18 0 0 0 f8 f8 6*18 1f 1f 0 0 0 18 18 18 f8 f8 6*0 ff ff 0 0 0 11*18 ff ff 6*0 ff
  //   ff 6*18 1f 1f 6*18 f8 f8 6*18 ff ff 18 18 18 1 3 6 c 18 30 60 c0 80 c0 60 30 18 c 6 3 c0 60 30 18 c
  //   6 3 1 3 6 c 18 30 60 c0 80 c3 66 2c 18 34 66 c3 81 0 0 18 3c 3c 18 4*0 18 24 24 18 0 0 10 38 7c fe
  //   7c 38 10 0 10 38 54 fe 54 10 38 0 44 ee fe fe 7c 38 10 0 10 38 7c fe 6c 10 38 0 0 2 0 0 10 1 5*0 8
  //   7*0 18 18 0 0 0 cc 66 33 99 cc 66 33 99 33 66 cc 99 33 66 cc 99 9*0 18 18 18 0 18 18 0 0 36 36 5*0
  //   36 36 7f 36 7f 36 36 0 8 3e 68 3e b 3e 8 0 21 52 24 8 12 25 42 0 30 48 68 30 5b 4c 36 0 18 18 30 5*0
  //   18 30 60 60 60 30 18 0 c 6 3 3 3 6 c 0 0 36 1c 7f 1c 36 0 0 0 c c 3f c c 6*0 18 18 30 5*0 3f 8*0 18
  //   18 0 0 3 6 c 18 30 60 0 0 3c 66 6e 76 66 3c 0 0 18 38 78 18 18 7e 0 0 3c 66 c 18 30 7e 0 0 3c 66 c 6
  //   66 3c 0 0 c 1c 2c 6c 7e c 0 0 7e 60 7c 6 66 3c 0 0 3c 60 7c 66 66 3c 0 0 7e 6 c 18 30 30 0 0 3c 66
  //   3c 66 66 3c 0 0 3c 66 66 3e 6 3c 0 0 0 c c 0 c c 0 0 0 c c 0 c 18 0 0 6 c 18 18 c 6 0 0 0 3e 0 3e
  //   4*0 30 18 c c 18 30 0 0 3c 66 c 18 0 18 0 1e 21 4d 55 4a 20 1e 0 0 3c 66 7e 66 66 66 0 0 7c 66 7c 66
  //   66 7c 0 0 3c 66 60 60 66 3c 0 0 78 6c 66 66 6c 78 0 0 7e 60 7c 60 60 7e 0 0 7e 60 7c 60 60 60 0 0 3c
  //   66 60 6e 66 3c 0 0 66 66 7e 66 66 66 0 0 7e 4*18 7e 0 0 3e c c c 6c 38 0 0 66 6c 78 78 6c 66 0 0
  //   5*60 7e 0 0 63 77 7f 6b 63 63 0 0 66 76 7e 6e 66 66 0 0 3c 4*66 3c 0 0 7c 66 66 7c 60 60 0 0 3c 66
  //   66 6a 6c 36 0 0 7c 66 66 7c 6c 66 0 0 3c 62 3c 6 66 3c 0 0 7e 5*18 0 0 5*66 3c 0 0 4*66 3c 18 0 0 63
  //   63 6b 7f 77 63 0 0 66 66 3c 3c 66 66 0 0 66 66 3c 18 18 18 0 0 7e c 18 30 60 7e 0 0 7c 4*60 7c 0 0
  //   60 30 18 c 6 3 0 0 3e 4*6 3e 0 0 18 3c 66 11*0 7f 0 60 30 18 6*0 3c 6 3e 66 3c 0 0 60 7c 66 66 66 7c
  //   0 0 0 3c 66 60 66 3c 0 0 6 3e 66 66 66 3e 0 0 0 3c 66 7c 60 3c 0 0 1e 30 7c 30 30 30 0 0 0 3c 66 66
  //   3e 6 3c 0 60 60 6c 76 66 66 0 0 18 0 38 18 18 3c 0 0 c 0 1c c c 6c 38 0 60 66 6c 78 6c 66 0 0 38
  //   4*18 3c 0 0 0 36 7f 6b 6b 63 0 0 0 7c 4*66 0 0 0 3c 66 66 66 3c 0 0 0 7c 66 66 7c 60 60 0 0 3e 66 66
  //   3e 6 6 0 0 6c 76 60 60 60 0 0 0 3c 60 3c 6 3c 0 0 30 7c 30 30 30 1c 0 0 0 4*66 3c 0 0 0 66 66 66 3c
  //   18 0 0 0 63 6b 6b 7f 36 0 0 0 66 3c 18 3c 66 0 0 0 66 66 66 3e 6 3c 0 0 7e c 18 30 7e 0 0 6 c c 18 c
  //   c 6 0 7*18 0 30 18 18 c 18 18 30 0 0 0 31 6b 46 5*0 18 24 42 42 7e 256*0 1 3 7 f 1f 3f 7f ff 80 c0
  //   e0 f0 f8 fc fe ff 4*0 1 3 7 f 4*0 80 c0 e0 f0 1 2 4 8 10 20 40 80 80 40 20 10 8 4 2 1 4*0 1 2 4 8
  //   4*0 80 40 20 10 0 3c 42 81 24 e7 3c 1 ff 7*80 ff 7*0 ff 7*1 ff 6*81 ff 18 24 42 81 81 42 24 18 18 18
  //   3c 3c 7e 7e ff ff 18 18 24 24 42 42 81 81 ff 7f 3f 1f f 7 3 1 ff fe fc f8 f0 e0 c0 80 f 7 3 1 4*0 f0
  //   e0 c0 80 4*0 80 40 20 10 8 4 2 1 1 2 4 8 10 20 40 80 8 4 2 1 4*0 10 20 40 80 4*0 e3 95 89 a2 bc a0
  //   a0 0 8*80 a5 0 81 0 0 81 0 a5 8*1 0 0 3c 24 24 3c 0 0 18 3c 7e ff ff 7e 3c 18 ff ff 7e 7e 3c 3c 18
  //   18 81 81 42 42 24 24 18 18 57*0 c a 9 4 2 1 0 0 30 50 90 20 40 80 0 7*80 ff 7*0 ff 7*1 ff 3 f 3f ff
  //   ff 3f f 3 c0 f0 fc ff ff fc f0 c0 3 c 30 c0 c0 30 c 3 c0 30 c 3 3 c 30 c0 20*0 f 8 8 8 4*0 ff 7*0 f0
  //   10 10 10 8*8 44 48 50 60 4*0 8*10 8 8 8 f 7*0 ff 4*0 10 10 10 f0 5*0 18 24 42 24 18 4*0 18 76 24 18
  //   5*0 2a 22 2 4*0 2 4c 30 7*0 42 3c 14*0 4*f 4*0 4*f0 4*0 4*ff 4*f 4*0 12*f 4*f0 4*f 4*ff 4*f0 4*0
  //   4*f0 4*f 12*f0 8*ff 4*0 4*ff 4*f 4*ff 4*f0 8*ff 8*0 8*3 8*c 8*f 8*30 8*33 8*3c 8*3f 8*c0 8*c3 8*cc
  //   8*cf 8*f0 8*f3 8*fc 8*ff
  //   CharROM
  //   Data ready by /CLK mid-cycle for VDP
  //   CharROM Output
  //   U55
  //   CharROM
  //   Bypass MUX
  //   U54
  //   contents of rom_2 (hex, n*v repeats v):
  //   78 d8 a9 10 85 de a2 0 86 cc 20 81 fe a0 0 20 1e fd a6 dd ca ca 86 cd 20 ec c7 a0 1c 20 1e fd 78 d8
  //   20 8e ff 20 90 c8 a0 3a 20 1e fd a2 ff 9a e8 86 9a a5 9a f0 e a5 98 85 cc a5 99 85 cd 20 ec c7 20 f8
  //   c7 20 8 fe 20 52 fd a0 0 84 5e 84 5f 20 ed c6 c9 0 f0 d5 a5 9a d0 17 20 2b c3 b0 12 a2 37 20 58 c3
  //   b0 27 20 a8 c0 a9 1 20 a1 c8 4c c5 c9 20 ed c6 c9 0 f0 28 20 a8 c0 20 8 c9 18 a5 98 65 9a 85 98 90
  //   aa e6 99 f0 a0 d0 a4 20 95 c0 4c 33 c0 29 f aa a9 c8 48 bd 5a c4 48 4c ed c6 20 55 c8 4c 2d c0 20 d2
  //   c0 a9 3a 20 4a c3 f0 f6 20 ca c0 4c 71 c1 a5 cd d0 9 a5 cc c9 a b0 3 4c d0 c7 a0 c1 4c e7 c4 a2 1b
  //   20 58 c3 b0 3f 60 a2 c6 20 62 c3 b0 f a9 22 20 4a c3 d0 d5 a9 9c 20 d0 c7 4c 82 c2 29 3f aa bd a6 c4
  //   a2 c1 85 c0 86 c1 6c c0 10*0 20 ca c7 20 2a c2 a2 0 20 58 c3 90 c5 4c 14 c3 a9 c9 20 d0 c7 68 68 20
  //   df c7 20 ca c7 4c 14 c3 20 3a c2 a2 5 20 58 c3 90 47 20 2a c2 a2 8 20 58 c3 90 53 4c 2a c2 20 e7 c2
  //   a5 9b c9 1 f0 31 60 a9 23 20 39 c3 20 fe cc 90 26 4c b8 c0 a2 d 20 58 c3 90 1c 20 42 c2 a9 28 20 4a
  //   c3 d0 8 20 42 c2 20 48 c3 f0 f8 a9 3d 20 4a c3 d0 19 4c e0 c0 a0 8c 4c e7 c4 20 e7 c2 a9 3d 20 39 c3
  //   20 82 c2 a5 9b c5 9c d0 5b 60 20 2a c2 20 37 c3 20 2a c2 20 37 c3 4c 2a c2 20 88 c1 20 9d c1 20 48
  //   c3 d0 e5 4c 2a c2 20 e7 c2 a9 24 20 4a c3 d0 3 20 d0 c7 a9 28 20 39 c3 4c 6 c3 20 ca c7 20 99 c3 4c
  //   df c7 20 ca c7 a9 0 85 9d 20 e7 c2 e6 9d 20 48 c3 f0 f6 a9 9d 4c e4 c7 20 41 c1 20 37 c3 4c 32 c2 a0
  //   b6 4c e7 c4 a6 90 20 57 c3 20 ca c0 20 e7 c2 4c e7 c1 20 c8 c3 4c e7 c1 a2 9b 20 57 c3 a2 10 20 58
  //   c3 b0 9 20 ca c0 20 82 c2 4c fb c1 29 bf 20 d0 c7 a9 28 20 4a c3 c9 ba d0 6 20 2a c2 20 37 c3 20 2a
  //   c2 4c fb c1 20 82 c2 a5 9b d0 b1 60 20 82 c2 a5 9b f0 a9 60 20 e7 c2 a5 9b d0 a1 60 20 e7 c2 a5 9b
  //   f0 99 60 e6 9c 60 20 2a c2 20 48 c3 90 52 4c 2a c2 4c 32 c2 20 4a c2 20 32 c2 4c 50 c2 20 5b c2 4c
  //   50 c2 20 4a c2 4c 2a c2 4c 46 c1 20 82 c2 a5 9c c9 1 f0 3 20 32 c2 4c 32 c2 a9 0 85 9c a2 6c 20 57
  //   c3 20 ed c6 aa 20 f7 c6 90 16 8a 20 c4 c7 90 28 b0 b a9 bb 20 d0 c7 20 c8 c3 4c c2 c2 4c 71 c1 a2 c7
  //   20 62 c3 b0 6 20 e7 c2 4c c2 c2 29 3f aa bd c9 c4 a2 c2 4c f0 c0 a2 75 20 57 c3 a2 20 20 58 c3 60 a2
  //   88 20 57 c3 a9 ac 20 d0 c7 4c 86 c2 a2 8b 20 57 c3 a9 aa 20 d0 c7 4c 86 c2 a9 0 85 9b 20 a8 c3 90 b7
  //   a9 24 20 4a c3 d0 5 20 d0 c7 e6 9b a9 28 20 4a c3 d0 10 20 d0 c7 20 2a c2 20 48 c3 f0 f8 a9 29 4c 39
  //   c3 60 20 fe cc 90 f a9 cc 20 d0 c7 a5 cc 20 d0 c7 a5 cd 4c d0 c7 4c d2 c0 20 fe cc a5 cc 85 98 a5 cd
  //   85 99 60 a9 2c 85 c6 20 ed c6 c5 c6 d0 1 60 a5 c6 4c ed c4 a9 2c 85 c6 20 ed c6 c5 c6 d0 3 c8 a2 0
  //   60 60 20 ed c6 a9 c4 85 c1 8a d0 11 20 ed c6 20 f7 c6 b0 2b 86 c1 aa a9 0 85 c0 b5 c0 85 c0 a2 0 84
  //   c6 88 c6 c0 c8 e6 c0 a1 c0 30 14 d9 0 1 f0 f4 e6 c0 a1 c0 10 fa e6 c0 a4 c6 a 30 e4 18 60 38 60 20
  //   ed c6 b9 0 1 f0 6 c8 20 d0 c7 10 f5 60 20 ed c6 aa 20 f7 c6 b0 16 8a 20 d0 c7 b9 0 1 c8 aa 20 f7 c6
  //   90 f2 8a 20 c4 c7 90 ec 88 18 60 88 d0 3 20 d0 c7 c8 b9 0 1 f0 b c9 22 d0 f3 c8 d9 0 1 f0 ed 60 a9
  //   22 4c ed c4 28*0 54 48 45 4e 80 54 4f 80 53 54 45 50 80 46 4e 80 53 50 43 f8 54 41 42 f9 41 54 fa 45
  //   4c 53 45 c9 41 4e 44 f0 4f 52 f1 45 4f 52 f2 44 49 56 f3 4d 4f 44 b4 4e 4f 54 b5 4c 49 53 54 c0 52
  //   55 4e c1 41 55 54 4f c2 41 52 54 c3 53 41 56 45 c4 44 45 4c c5 4e 45 57 c6 4f 4c 44 87 0 84 5f 2 1
  //   34 8f 9f 87 f5 e7 fb 86 9c cd da 17 e7 2d a1 2b 4 28 a0 22 5 84 2b a2 2d a3 2a a4 2f a5 5e a6 3d a8
  //   29 9 3e 6 3c 7 84 3d ad 84 3d ab 3e a9 84 22 1 2c 80 3b 80 3a 40 0 40 82 2c 80 3b 81 27 82 3a 40 0
  //   40 83 87 87 87 41 87 ba 8e a5 4e 17 87 20 94 94 0 e7 76 df 8e 94 37 8e d9 88 fb 8e 8e c3 87 94 87 ba
  //   97 94 94 6*4c 9*55 4d 58 58 58 4a 73 5b 5b 5b 64 6a 6a 70 70 41 20 1e fd 4c 2d c0 48 a0 83 20 24 fd
  //   68 20 66 fd 20 52 fd 4c 2d c0 0 0 0 1b 92 93 94 95 96 90 d d 46 72 6f 6e 74 69 65 72 20 42 41 53 49
  //   43 20 31 2e 30 d 1d 20 62 79 74 65 73 20 66 72 65 65 d 54 79 70 65 20 41 52 54 20 74 6f 20 64 72 61
  //   77 d 5 52 65 61 64 79 9 53 65 61 72 63 68 69 6e 67 7 4c 6f 61 64 69 6e 67 20 41 52 54 20 ac ad ae af
  //   20 6d 6f 76 65 20 47 52 41 20 64 72 61 77 20 43 4f 4c 20 63 6f 6c 6f 72 4 50 4c 41 59 4 53 54 4f 50
  //   5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
  //   Row of 32
  //   VDP read during first half of CLK
  //   Data from memory latched at /CLK
  //   U45-U57 (+U39)
  //   U39 8-bit Shift Register
  //   U53
  //   VDP Latch
  //   Latched at /CLK
  //   VDP Latch Output
  //   5 Pixel Pipe + 7 Color/2bpp
  //   U45 Dual D-FF 74LS74 (Delay/Clocking)
  //   U53 8-bit Register 74LS273 (VDP Latch)
  //   U54 Quad 1-of-2 MUX 74LS157 (Char Bypass MUX)
  //   U55 Quad 1-of-2 MUX 74LS157 (Char Bypass MUX)
  //   U46 Dual 1-of-4 74LS153 (Palette MUX)
  //   U47 Dual 1-of-4 74LS153 (Palette MUX)
  //   U48 4-bit DFF with Clear 74LS175 (FG)
  //   U49 4-bit DFF with Clear 74LS175 (BG)
  //   U50 Quad 1-of-2 MUX 74LS157 (FG)
  //   U51 Quad 1-of-2 MUX 74LS157 (BG)
  //   U52 8-bit Register 74LS273 (Color 2/3)
  //   U56 Triple 3-AND 74LS11 (Color Decode)
  //   U57 Quad 2-AND 74LS08 (Color Decode)
  //   U58 Quad 2-OR 74LS32 (Color Decode)
  //   U59 Hex NOT 74LS04 (Color Decode)
  //   Data Bus
  //   Latch data at /CLK for VDP
  //   Video Out
  //   PCLK
  //   HSync
  //   Burst
  //   VSync
  //   Color
  //   Pixel Color
  //   VSync
  //   VSync
  //   HSync
  //   Vpos
  //   Hpos
  //   PCLK / Hsync
  //   Hsync / Vsync
  //   Most home computers/consoles use 0 IRE
  //   for both Black and Blanking level
endmodule

// DBUS
module PSG (
  input  HSync,
  input  nPHI2,
  input  nWR,
  input  [7:0] DBUS,
  output SND
);

  wire CounterHi_pin1, CounterHi_pin7, CounterHi_pin9, CounterHi_pin15, CounterLo_pin1, CounterLo_pin7,
       FreqLatch_pin2, FreqLatch_pin5, FreqLatch_pin6, FreqLatch_pin9, FreqLatch_pin12, FreqLatch_pin15,
       FreqLatch_pin16, FreqLatch_pin19;

  _74377 #(.ShowInternalStructure("true")) FreqLatch (
    .pin1(nWR), .pin2(FreqLatch_pin2), .pin3(DBUS[0]), .pin4(DBUS[1]), .pin5(FreqLatch_pin5),
    .pin6(FreqLatch_pin6), .pin7(DBUS[2]), .pin8(DBUS[3]), .pin9(FreqLatch_pin9), .pin19(FreqLatch_pin19),
    .pin18(DBUS[7]), .pin17(DBUS[6]), .pin16(FreqLatch_pin16), .pin15(FreqLatch_pin15), .pin14(DBUS[5]),
    .pin13(DBUS[4]), .pin12(FreqLatch_pin12), .pin11(nPHI2));
  _74161 #(.ShowInternalStructure("true")) CounterHi (
    .pin1(CounterHi_pin1), .pin2(HSync), .pin3(FreqLatch_pin12), .pin4(FreqLatch_pin15),
    .pin5(FreqLatch_pin16), .pin6(FreqLatch_pin19), .pin7(CounterHi_pin7), .pin15(CounterHi_pin15),
    .pin10(CounterHi_pin7), .pin9(CounterHi_pin9));  // open: pin14, pin13, pin12, pin11
  _74161 #(.ShowInternalStructure("true")) CounterLo (
    .pin1(CounterLo_pin1), .pin2(HSync), .pin3(FreqLatch_pin2), .pin4(FreqLatch_pin5), .pin5(FreqLatch_pin6),
    .pin6(FreqLatch_pin9), .pin7(CounterLo_pin7), .pin15(CounterHi_pin7), .pin10(CounterLo_pin7),
    .pin9(CounterHi_pin9));  // open: pin14, pin13, pin12, pin11
  not not_1 (CounterHi_pin9, CounterHi_pin15);
  T_Flip_Flop t_ff_1 (.clk(HSync), .T(CounterHi_pin15), .Q(SND));  // open: Qn, preset, reset
  LED led_1 (.in(SND));
  // also tied to VCC on the sheet: {CounterHi_pin1, CounterLo_pin1, CounterLo_pin7}

  // Notes on the sheet:
  //   nWR: initial=0x1
  //   DBUS: initial=0x80
  //   Note: if using 374, NOR nWR with nPHI2
  //   IO address decode
  //   Rising Edge as PHI2 falls
  //   74LS374 ?
  //   15720 Hz
  //   DIV 2
endmodule

module SN74LS298 (
  input  WS,
  input  A1,
  input  B1,
  input  C1,
  input  D1,
  input  A2,
  input  B2,
  input  C2,
  input  D2,
  input  CLK,
  output QA,
  output QB,
  output QC,
  output QD
);

  wire n74157_1_pin4, n74157_1_pin7, n74157_1_pin9, n74157_1_pin12, n74157_1_pin15, n74175_1_pin1;

  _74157 #(.ShowInternalStructure("true")) u_74157_1 (
    .pin1(WS), .pin2(A1), .pin3(A2), .pin4(n74157_1_pin4), .pin5(B1), .pin6(B2), .pin7(n74157_1_pin7),
    .pin15(n74157_1_pin15), .pin14(D1), .pin13(D2), .pin12(n74157_1_pin12), .pin11(C1), .pin10(C2),
    .pin9(n74157_1_pin9));
  _74175 #(.ShowInternalStructure("true")) u_74175_1 (
    .pin1(n74175_1_pin1), .pin2(QA), .pin4(n74157_1_pin4), .pin5(n74157_1_pin7), .pin7(QB), .pin15(QD),
    .pin13(n74157_1_pin12), .pin12(n74157_1_pin9), .pin10(QC), .pin9(CLK));  // open: pin3, pin6, pin14, pin11
  // also tied to GND on the sheet: n74157_1_pin15
  // also tied to VCC on the sheet: n74175_1_pin1

  // Notes on the sheet:
  //   74LS175
endmodule

// 555
module Timer_555 (
  input  [7:0] Count,
  input  Trigger,
  output DOut
);

  wire clock_1_out, counter_1_carry, not_1_out;

  Clock clock_1 (.out(clock_1_out));
  not not_1 (not_1_out, Trigger);
  Counter counter_1 (
    .load(not_1_out), .D(Count), .count(DOut), .carry(counter_1_carry), .clk(clock_1_out));  // open: Q, up, clr
  J_K_Flip_Flop j_k_ff_1 (.J(not_1_out), .clk(clock_1_out), .K(counter_1_carry), .Q(DOut));  // open: Qn, preset, reset

  // Notes on the sheet:
  //   555 triggers
  //   on falling edge
  //   14.31818 MHz
endmodule

// 393
module SN74LS393 (
  input  nCLK1,
  input  CLR1,
  input  nCLK2,
  input  CLR2,
  output QA,
  output QB,
  output QC,
  output QD,
  output QE,
  output QF,
  output QG,
  output QH
);

  wire not_1_out, not_2_out, t_ff_1_qn, t_ff_2_qn, t_ff_3_qn, t_ff_5_qn, t_ff_6_qn, t_ff_7_qn;

  not not_1 (not_1_out, nCLK1);
  not not_2 (not_2_out, nCLK2);
  T_Flip_Flop t_ff_1 (.clk(not_1_out), .T(1'b1), .Q(QA), .Qn(t_ff_1_qn), .reset(CLR1));  // open: preset
  T_Flip_Flop t_ff_2 (.clk(t_ff_1_qn), .T(1'b1), .Q(QB), .Qn(t_ff_2_qn), .reset(CLR1));  // open: preset
  T_Flip_Flop t_ff_3 (.clk(t_ff_2_qn), .T(1'b1), .Q(QC), .Qn(t_ff_3_qn), .reset(CLR1));  // open: preset
  T_Flip_Flop t_ff_4 (.clk(t_ff_3_qn), .T(1'b1), .Q(QD), .reset(CLR1));  // open: Qn, preset
  T_Flip_Flop t_ff_5 (.clk(not_2_out), .T(1'b1), .Q(QE), .Qn(t_ff_5_qn), .preset(1'b0), .reset(CLR2));
  T_Flip_Flop t_ff_6 (.clk(t_ff_5_qn), .T(1'b1), .Q(QF), .Qn(t_ff_6_qn), .preset(1'b0), .reset(CLR2));
  T_Flip_Flop t_ff_7 (.clk(t_ff_6_qn), .T(1'b1), .Q(QG), .Qn(t_ff_7_qn), .preset(1'b0), .reset(CLR2));
  T_Flip_Flop t_ff_8 (.clk(t_ff_7_qn), .T(1'b1), .Q(QH), .preset(1'b0), .reset(CLR2));  // open: Qn
endmodule
